// Logisim project Labb 3.circ as structural Verilog: 1 circuit, main circuit main
module main (
  input  B,
  input  A
);

  wire and_1_out, and_2_out, and_3_out, clock_1_out, nor_1_out, nor_2_out, nor_3_out, nor_4_out, not_1_out,
       not_2_out, not_3_out, not_4_out, not_5_out, not_6_out, or_1_out, or_2_out, or_3_out, or_4_out, Q0_q,
       Q0_qn, Q1_q, Q1_qn;

  not not_1 (not_1_out, B);
  not not_2 (not_2_out, A);
  and and_1 (and_1_out, Q1_qn, not_1_out);
  and and_2 (and_2_out, Q1_q, Q0_qn, B);
  or or_1 (or_1_out, B, not_2_out);
  nor nor_1 (nor_1_out, Q0_qn, Q1_q);
  not not_3 (not_3_out, nor_1_out);
  nor nor_2 (nor_2_out, A, Q0_q);
  nor nor_3 (nor_3_out, not_1_out, Q1_qn);
  or or_2 (or_2_out, or_1_out, not_3_out);
  not not_4 (not_4_out, nor_4_out);
  not not_5 (not_5_out, nor_2_out);
  nor nor_4 (nor_4_out, not_5_out, Q1_q);
  not not_6 (not_6_out, nor_3_out);
  or or_3 (or_3_out, and_1_out, and_2_out);
  or or_4 (or_4_out, or_3_out, not_2_out);
  Clock clock_1 (.out(clock_1_out));
  and and_3 (and_3_out, or_2_out, not_4_out, not_6_out);
  D_Flip_Flop Q1 (.clk(clock_1_out), .D(or_4_out), .Q(Q1_q), .Qn(Q1_qn), .preset(and_3_out), .reset(1'b0));  // open: en
  D_Flip_Flop Q0 (
    .clk(clock_1_out), .D(and_3_out), .Q(Q0_q), .Qn(Q0_qn), .preset(and_3_out), .reset(1'b0));  // open: en
endmodule
