// Logisim project NAND Test.circ as structural Verilog: 1 circuit, main circuit main
module main (
);

  wire nand_1_out, nand_2_out, nand_3_out, not_1_out, not_2_out, not_3_out, or_1_out, undriven, undriven_2,
       undriven_3, undriven_4, undriven_5, undriven_6, undriven_7;

  not not_1 (not_1_out, undriven);
  not not_2 (not_2_out, undriven_2);
  not not_3 (not_3_out, undriven_3);
  nand nand_1 (nand_1_out, undriven_4, undriven_5);
  nand nand_2 (nand_2_out, undriven_6, undriven_7);
  or or_1 (or_1_out, not_1_out, not_2_out, not_3_out);
  nand nand_3 (nand_3_out, nand_1_out, nand_2_out, or_1_out);
endmodule
